# Fritzing sketch Untitled Sketch (saved by Fritzing 0.9.3b)
breadboards: 2

parts:
  Mod1 = ESP32 - CAM
  Componente1 = FTDI Basic Programmer
  LED2 = smd LED [color="Blue (430nm)" package="1206 [SMD]"]  # not connected
  R1 = Resistor [tolerance=±5% resistance=330 package=THT]

nets:
  N1: Mod1.5V, Componente1.POWER
  GND: Mod1.GND, Mod1.IO0, Componente1.GND, R1.Pin_0
  N2: Mod1.VOT, Componente1.RXI
  N3: Mod1.VOR, Componente1.TXO

custom parts:
  ESP32 - CAM: The ESP32-CAM has a very competitive small-size camera module that can operate independently as a minimum system with a footprint of only 27*40.5*4.5mm and a deep sleep current of up to 6mA.
